// Logisim project 1001checker.circ as structural Verilog: 3 circuits, main circuit 状态转移
module \状态转移  (
  input  S0,
  input  S1,
  input  S2,
  input  in,
  output N0,
  output N1,
  output N2
);

  wire and_1_out, and_2_out, and_3_out, and_4_out, and_5_out, and_6_out, and_7_out, and_8_out, not_1_out,
       not_2_out, not_3_out, not_4_out, not_5_out, not_6_out, not_7_out, not_8_out, not_9_out, not_10_out,
       not_11_out, not_12_out, not_13_out, not_14_out, not_15_out, not_16_out, not_17_out, not_18_out,
       not_19_out, not_20_out, not_21_out, not_22_out;

  not not_1 (not_1_out, S2);
  not not_2 (not_2_out, S0);
  not not_3 (not_3_out, in);
  not not_4 (not_4_out, S2);
  not not_5 (not_5_out, S1);
  not not_6 (not_6_out, S0);
  not not_7 (not_7_out, S2);
  not not_8 (not_8_out, S1);
  not not_9 (not_9_out, S2);
  not not_10 (not_10_out, S0);
  not not_11 (not_11_out, S1);
  not not_12 (not_12_out, S0);
  not not_13 (not_13_out, S2);
  not not_14 (not_14_out, S1);
  not not_15 (not_15_out, in);
  not not_16 (not_16_out, S2);
  not not_17 (not_17_out, S0);
  not not_18 (not_18_out, in);
  not not_19 (not_19_out, S1);
  not not_20 (not_20_out, S0);
  not not_21 (not_21_out, in);
  not not_22 (not_22_out, S2);
  and and_1 (and_1_out, not_1_out, S1, not_2_out, not_3_out);
  and and_2 (and_2_out, not_4_out, not_5_out, not_6_out, in);
  and and_3 (and_3_out, not_7_out, not_8_out, S0, in);
  and and_4 (and_4_out, not_9_out, S1, not_10_out, in);
  and and_5 (and_5_out, S2, not_11_out, not_12_out, in);
  and and_6 (and_6_out, not_13_out, not_14_out, S0, not_15_out);
  and and_7 (and_7_out, not_16_out, S1, not_17_out, not_18_out);
  or or_1 (N1, and_6_out, and_7_out, and_8_out);
  and and_8 (and_8_out, S2, not_19_out, not_20_out, not_21_out);
  and and_9 (N2, not_22_out, S1, S0, in);
  or or_2 (N0, and_1_out, and_2_out, and_3_out, and_4_out, and_5_out);
endmodule

module \_1001检测  (
  input  S0,
  input  S1,
  input  S2,
  output out
);

  wire not_1_out, not_2_out;

  not not_1 (not_1_out, S0);
  not not_2 (not_2_out, S1);
  and and_1 (out, not_1_out, not_2_out, S2);
endmodule

module \检测器  (
  input  in_1,
  output out_2
);

  wire clk, rst;
  wire [2:0] d_ff_1_q, \状态转移_1_n0 ;

  Clock #(.highDuration(1), .lowDuration(1)) clock_1 (.out(clk));
  Button button_1 (.out(rst));
  D_Flip_Flop #(.trigger("rising"), .Pre_Clr_Positions("ABOVE_BELOW"), .NegatePresetClear("false"), .enable("false"), .NewFFLayout("true")) d_ff_1 (
    .clk(clk), .D(\状态转移_1_n0 [0]), .Q(d_ff_1_q[0]), .reset(rst));  // open: Qn, preset
  D_Flip_Flop #(.trigger("rising"), .Pre_Clr_Positions("ABOVE_BELOW"), .NegatePresetClear("false"), .enable("false"), .NewFFLayout("true")) d_ff_2 (
    .clk(clk), .D(\状态转移_1_n0 [1]), .Q(d_ff_1_q[1]), .reset(rst));  // open: Qn, preset
  D_Flip_Flop #(.trigger("rising"), .Pre_Clr_Positions("ABOVE_BELOW"), .NegatePresetClear("false"), .enable("false"), .NewFFLayout("true")) d_ff_3 (
    .clk(clk), .D(\状态转移_1_n0 [2]), .Q(d_ff_1_q[2]), .reset(rst));  // open: Qn, preset
  // Probe on d_ff_1_q
  \_1001检测  \u_1001检测_1  (.S0(d_ff_1_q[0]), .S1(d_ff_1_q[1]), .S2(d_ff_1_q[2]), .out(out_2));
  // Probe on \状态转移_1_n0 
  \状态转移  \u_状态转移_1  (
    .S0(d_ff_1_q[0]), .S1(d_ff_1_q[1]), .S2(d_ff_1_q[2]), .in(in_1), .N0(\状态转移_1_n0 [0]),
    .N1(\状态转移_1_n0 [1]), .N2(\状态转移_1_n0 [2]));

  // Other names for the same wires on the sheet: in = in_1; out = out_2
endmodule
